// Digital circuit CPU.dig as structural Verilog
module CPU (
  input  clk,
  input  RUN
);

  wire A_LD_CDATA, A_OUT_CDATA, ALU_NOUT, ALU_VOUT, ALUA_LD_CDATA, ALUB_LD_CDATA, ALUC_LD, ALUC_OUT,
       ALUC_SRC_0, ALUC_SRC_1, ALUOP_0, ALUOP_1, ALUOP_2, ALUOP_3, ALUR_OUT_CDATA, ALUZ_OUT, and_1_out,
       and_2_out, C, CDATA_LD_0, CDATA_LD_FF, CDATA_TO_CADDRH, CDATA_TO_CADDRL, Clck0, Clck1, clock_1_cout,
       CS0, CS1, CS3, CUP_SRC_ALU, decoder_1_out_0, decoder_1_out_1, decoder_1_out_2, decoder_1_out_3,
       decoder_1_out_4, decoder_1_out_5, decoder_1_out_6, decoder_1_out_7, ERR, HALT, HALTED, IR_LD_XDATA,
       lt_ALUC_gt, MARH_LD_CADDRH, MARL_LD_CADDRL, MBR_LD_CDATA, MBR_LD_XDATA, MBR_OUT_CDATA, MBR_OUT_XDATA,
       MEM_LD_XDATA, MEM_OUT_XDATA, multiplexer_2_out, multiplexer_3_out, multiplexer_4_out,
       multiplexer_5_out, multiplexer_6_out, N, nor_1_out, or_1_out, or_3_out, or_4_out, or_5_out, or_6_out,
       P_SRC_0, P_SRC_1, PC_ADD_CDATA, PC_INC, PC_LD, PC_OUT_CADDR, PCH_LD_CDATA, PCH_OUT_CDATA,
       PCL_LD_CDATA, PCL_OUT_CDATA, PN_LD, PV_LD, PZ_LD, RESET, S_DEC, S_INC, S_LD_CDATA, S_OUT_CADDR,
       S_OUT_CDATA, STASHH_LD_CDATA, STASHH_OUT_CDATA, STASHL_LD_CDATA, STASHL_OUT_CDATA, STEP_out, V,
       X_LD_CDATA, X_OUT_CDATA, Y_LD_CDATA, Y_OUT_CDATA, Z;
  wire [2:0] lt_uNEXTMUX_gt;
  wire [3:0] multiplexer_7_out;
  wire [7:0] A, ALUR, CADDRH, CADDRL, CDATA, IR, lt_ALUA_gt, lt_ALUB_gt, MARH, MARL, MBR, multiplexer_1_out,
       PCH, PCL, RAM_d, S, STASHH, STASHL, X, Y;
  wire [15:0] DEMODE, DEOPCODE, lt_uCAR_gt, lt_uNEXTCAR_gt, lt_uParam_gt;

  Button STEP (.out(STEP_out));
  Button u_RESET (.out(RESET));
  or or_1 (or_1_out, HALT, ERR);
  Seven_Seg_Hex seven_seg_hex_1 (.d(MARH[7:4]), .dp(1'b0));
  Clock clock_1 (.RUN(RUN), .STEP(STEP_out), .HALT(or_1_out), .Cin(clk), .HALTED(HALTED), .Cout(clock_1_cout));
  Seven_Seg_Hex seven_seg_hex_2 (.d(MARL[7:4]), .dp(1'b0));
  Seven_Seg_Hex seven_seg_hex_3 (.d(MARH[3:0]), .dp(1'b0));
  Seven_Seg_Hex seven_seg_hex_4 (.d(A[3:0]), .dp(1'b0));
  Seven_Seg_Hex seven_seg_hex_5 (.d(A[7:4]), .dp(1'b0));
  and and_1 (and_1_out, HALTED, RESET);
  Seven_Seg_Hex seven_seg_hex_6 (.d(MARL[3:0]), .dp(1'b0));
  Seven_Seg_Hex seven_seg_hex_7 (.d(X[3:0]), .dp(1'b0));
  Seven_Seg_Hex seven_seg_hex_8 (.d(X[7:4]), .dp(1'b0));
  Seven_Seg_Hex seven_seg_hex_9 (.d(MBR[3:0]), .dp(1'b0));
  Seven_Seg_Hex seven_seg_hex_10 (.d(MBR[7:4]), .dp(1'b0));
  Seven_Seg_Hex seven_seg_hex_11 (.d(Y[7:4]), .dp(1'b0));
  or or_2 (Clck1, clock_1_cout, and_1_out);
  Seven_Seg_Hex seven_seg_hex_12 (.d(PCH[3:0]), .dp(1'b0));
  Seven_Seg_Hex seven_seg_hex_13 (.d(PCH[7:4]), .dp(1'b0));
  Seven_Seg_Hex seven_seg_hex_14 (.d(Y[3:0]), .dp(1'b0));
  not not_1 (Clck0, Clck1);
  Seven_Seg_Hex seven_seg_hex_15 (.d(PCL[3:0]), .dp(1'b0));
  Seven_Seg_Hex seven_seg_hex_16 (.d(PCL[7:4]), .dp(1'b0));
  Seven_Seg_Hex seven_seg_hex_17 (.d(IR[7:4]), .dp(1'b0));
  LED led_1 (.in(N));
  LED led_2 (.in(V));
  Seven_Seg_Hex seven_seg_hex_18 (.d(IR[3:0]), .dp(1'b0));
  Seven_Seg_Hex seven_seg_hex_19 (.d(STASHL[7:4]), .dp(1'b0));
  LED led_3 (.in(Z));
  Seven_Seg_Hex seven_seg_hex_20 (.d(STASHL[3:0]), .dp(1'b0));
  LED led_4 (.in(C));
  Seven_Seg_Hex seven_seg_hex_21 (.d(STASHH[3:0]), .dp(1'b0));
  Seven_Seg_Hex seven_seg_hex_22 (.d(STASHH[7:4]), .dp(1'b0));
  Seven_Seg_Hex seven_seg_hex_23 (.d(S[3:0]), .dp(1'b0));
  Seven_Seg_Hex seven_seg_hex_24 (.d(S[7:4]), .dp(1'b0));
  LED led_5 (.in(HALTED));
  LED led_6 (.in(ERR));
  or or_3 (or_3_out, MEM_LD_XDATA, MEM_OUT_XDATA);
  Address_Decoder address_decoder_1 (.A({MARH, MARL}), .CS(or_3_out), .CS0(CS0), .CS1(CS1), .CS3(CS3));  // open: CS2
  Register #(.Bits(8)) MAR_H (.D(CADDRH), .C(Clck0), .en(MARH_LD_CADDRH), .Q(MARH));
  Register #(.Bits(8)) MAR_L (.D(CADDRL), .C(Clck0), .en(MARL_LD_CADDRL), .Q(MARL));
  Seven_Seg_Hex seven_seg_hex_25 (.d(DEMODE[11:8]), .dp(1'b0));
  Seven_Seg_Hex seven_seg_hex_26 (.d(DEMODE[15:12]), .dp(1'b0));
  Seven_Seg_Hex seven_seg_hex_27 (.d(lt_ALUA_gt[3:0]), .dp(1'b0));
  Seven_Seg_Hex seven_seg_hex_28 (.d(lt_ALUA_gt[7:4]), .dp(1'b0));
  Seven_Seg_Hex seven_seg_hex_29 (.d(DEMODE[3:0]), .dp(1'b0));
  Seven_Seg_Hex seven_seg_hex_30 (.d(DEMODE[7:4]), .dp(1'b0));
  Seven_Seg_Hex seven_seg_hex_31 (.d(lt_ALUB_gt[3:0]), .dp(1'b0));
  Seven_Seg_Hex seven_seg_hex_32 (.d(lt_ALUB_gt[7:4]), .dp(1'b0));
  and and_2 (and_2_out, MEM_LD_XDATA, Clck1);
  assign CADDRH = CDATA_TO_CADDRH ? CDATA : 8'bz;  // Driver driver_1
  assign CADDRL = CDATA_TO_CADDRL ? CDATA : 8'bz;  // Driver driver_2
  Seven_Seg_Hex seven_seg_hex_33 (.d(DEOPCODE[11:8]), .dp(1'b0));
  Seven_Seg_Hex seven_seg_hex_34 (.d(DEOPCODE[15:12]), .dp(1'b0));
  LED led_7 (.in(lt_ALUC_gt));
  nor nor_1 (nor_1_out, CDATA[0], CDATA[1], CDATA[2], CDATA[3], CDATA[4], CDATA[5], CDATA[6], CDATA[7]);
  Seven_Seg_Hex seven_seg_hex_35 (.d(DEOPCODE[3:0]), .dp(1'b0));
  Seven_Seg_Hex seven_seg_hex_36 (.d(DEOPCODE[7:4]), .dp(1'b0));
  Seven_Seg_Hex seven_seg_hex_37 (.d(ALUR[3:0]), .dp(1'b0));
  Seven_Seg_Hex seven_seg_hex_38 (.d(ALUR[7:4]), .dp(1'b0));
  RAMSinglePortSel #(.AddrBits(14), .isProgramMemory("true"), .Bits(8)) RAM (
    .A({MARH[5:0], MARL}), .CS(CS0), .WE(and_2_out), .OE(MEM_OUT_XDATA), .D(RAM_d));
  Terminal terminal_1 (.D(RAM_d), .C(Clck1), .en(CS1));
  ROM #(.AddrBits(14), .Bits(8)) ROM (.A({MARH[5:0], MARL}), .sel(CS3), .D(RAM_d));
  Multiplexer #(.Bits(8)) multiplexer_1 (.sel(MBR_LD_CDATA), .in_0(RAM_d), .in_1(CDATA), .out(multiplexer_1_out));
  Register #(.Bits(8)) u_MBR (.D(multiplexer_1_out), .C(Clck1), .en(or_4_out), .Q(MBR));
  or or_4 (or_4_out, MBR_LD_CDATA, MBR_LD_XDATA);
  Multiplexer #(.Selector_Bits(2)) multiplexer_2 (
    .sel({P_SRC_1, P_SRC_0}), .in_0(1'b0), .in_1(1'b1), .in_2(ALUZ_OUT), .in_3(nor_1_out),
    .out(multiplexer_2_out));
  Seven_Seg_Hex seven_seg_hex_39 (.d(lt_uCAR_gt[15:12]), .dp(1'b0));
  LED led_8 (.in(ALU_NOUT));
  Multiplexer #(.Selector_Bits(2)) multiplexer_3 (
    .sel({P_SRC_1, P_SRC_0}), .in_0(1'b0), .in_1(1'b1), .in_2(ALU_VOUT), .in_3(1'b0), .out(multiplexer_3_out));
  Seven_Seg_Hex seven_seg_hex_40 (.d(lt_uCAR_gt[7:4]), .dp(1'b0));
  Seven_Seg_Hex seven_seg_hex_41 (.d(lt_uCAR_gt[11:8]), .dp(1'b0));
  LED led_9 (.in(ALU_VOUT));
  LED led_10 (.in(ALUZ_OUT));
  assign RAM_d = MBR_OUT_XDATA ? MBR : 8'bz;  // Driver driver_3
  assign CDATA = MBR_OUT_CDATA ? MBR : 8'bz;  // Driver driver_4
  Seven_Seg_Hex seven_seg_hex_42 (.d(lt_uCAR_gt[3:0]), .dp(1'b0));
  LED led_11 (.in(ALUC_OUT));
  Multiplexer #(.Selector_Bits(2)) multiplexer_4 (
    .sel({ALUC_SRC_1, ALUC_SRC_0}), .in_0(1'b0), .in_1(1'b1), .in_2(C), .in_3(C), .out(multiplexer_4_out));
  Multiplexer #(.Selector_Bits(2)) multiplexer_5 (
    .sel({P_SRC_1, P_SRC_0}), .in_0(1'b0), .in_1(1'b1), .in_2(ALU_NOUT), .in_3(CDATA[7]),
    .out(multiplexer_5_out));
  Multiplexer #(.Selector_Bits(2)) multiplexer_6 (
    .sel({P_SRC_1, P_SRC_0}), .in_0(1'b0), .in_1(1'b1), .in_2(ALUC_OUT), .in_3(1'b0), .out(multiplexer_6_out));
  Seven_Seg_Hex seven_seg_hex_43 (.d(lt_uNEXTCAR_gt[11:8]), .dp(1'b0));
  Seven_Seg_Hex seven_seg_hex_44 (.d(lt_uNEXTCAR_gt[15:12]), .dp(1'b0));
  Seven_Seg_Hex seven_seg_hex_45 (.d(lt_uNEXTCAR_gt[3:0]), .dp(1'b0));
  Seven_Seg_Hex seven_seg_hex_46 (.d(lt_uNEXTCAR_gt[7:4]), .dp(1'b0));
  Latched_ALU ALU (
    .CLOCK(Clck1), .A(CDATA), .B(CDATA), .CIN(multiplexer_4_out), .LDA(ALUA_LD_CDATA), .LDB(ALUB_LD_CDATA),
    .LDC(ALUC_LD), .OP({ALUOP_3, ALUOP_2, ALUOP_1, ALUOP_0}), .N(ALU_NOUT), .V(ALU_VOUT), .Z(ALUZ_OUT),
    .C(ALUC_OUT), .R(ALUR), .lt_A_gt(lt_ALUA_gt), .lt_B_gt(lt_ALUB_gt), .lt_C_gt(lt_ALUC_gt));
  Register PN (.D(multiplexer_5_out), .C(Clck1), .en(PN_LD), .Q(N));
  Register PV (.D(multiplexer_3_out), .C(Clck1), .en(PV_LD), .Q(V));
  Register PZ (.D(multiplexer_2_out), .C(Clck1), .en(PZ_LD), .Q(Z));
  Register PC (.D(multiplexer_6_out), .C(Clck1), .en(PC_LD), .Q(C));
  Seven_Seg_Hex seven_seg_hex_47 (.d(lt_uParam_gt[15:12]), .dp(1'b0));
  Register #(.Bits(8)) u_IR (.D(RAM_d), .C(Clck1), .en(IR_LD_XDATA), .Q(IR));
  Seven_Seg_Hex seven_seg_hex_48 (.d(lt_uParam_gt[7:4]), .dp(1'b0));
  Seven_Seg_Hex seven_seg_hex_49 (.d(lt_uParam_gt[11:8]), .dp(1'b0));
  Seven_Seg_Hex seven_seg_hex_50 (.d(lt_uParam_gt[3:0]), .dp(1'b0));
  assign CDATA = ALUR_OUT_CDATA ? ALUR : 8'bz;  // Driver driver_5
  Decoder #(.Selector_Bits(3)) decoder_1 (
    .sel(lt_uNEXTMUX_gt), .out_0(decoder_1_out_0), .out_1(decoder_1_out_1), .out_2(decoder_1_out_2),
    .out_3(decoder_1_out_3), .out_4(decoder_1_out_4), .out_5(decoder_1_out_5), .out_6(decoder_1_out_6),
    .out_7(decoder_1_out_7));
  or or_5 (or_5_out, S_LD_CDATA, S_INC, S_DEC);
  Multiplexer #(.Bits(4)) multiplexer_7 (
    .sel(CUP_SRC_ALU), .in_0({C, Z, V, N}), .in_1({ALUC_OUT, ALUZ_OUT, ALU_VOUT, ALU_NOUT}),
    .out(multiplexer_7_out));
  CounterPreset #(.Bits(8)) counterpreset_1 (
    .en(or_5_out), .C(Clck1), .dir(S_DEC), .in(CDATA), .ld(S_LD_CDATA), .clr(1'b0), .out(S));  // open: ovf
  Register u_STASHH (.C(Clck1), .D(CDATA), .OUT(STASHH_OUT_CDATA), .LD(STASHH_LD_CDATA), .Q(CDATA), .lt_Q_gt(STASHH));
  or or_6 (or_6_out, decoder_1_out_4, decoder_1_out_5, decoder_1_out_6, decoder_1_out_7);
  Control_Unit Control_Unit (
    .DEMODEin(DEMODE), .DEOPCODEin(DEOPCODE), .Nin(multiplexer_7_out[0]), .Vin(multiplexer_7_out[1]),
    .Zin(multiplexer_7_out[2]), .Cin(multiplexer_7_out[3]), .RESET(RESET), .ClockIn(Clck1),
    .lt_uCAR_gt(lt_uCAR_gt), .lt_uParam_gt(lt_uParam_gt), .lt_uNEXTCAR_gt(lt_uNEXTCAR_gt),
    .lt_uNEXTMUX_gt(lt_uNEXTMUX_gt), .HALT(HALT), .CDATA_LD_0(CDATA_LD_0), .CDATA_LD_FF(CDATA_LD_FF),
    .CDATA_TO_CADDRL(CDATA_TO_CADDRL), .CD_TO_CADDRH(CDATA_TO_CADDRH), .MEM_LD_XDATA(MEM_LD_XDATA),
    .MEM_OUT_XDATA(MEM_OUT_XDATA), .IR_LD_XDATA(IR_LD_XDATA), .MBR_LD_XDATA(MBR_LD_XDATA),
    .MBR_OUT_XDATA(MBR_OUT_XDATA), .MBR_LD_CDATA(MBR_LD_CDATA), .MBR_OUT_CDATA(MBR_OUT_CDATA),
    .MARL_LD_CADDRL(MARL_LD_CADDRL), .MARH_LD_CADDRH(MARH_LD_CADDRH), .PC_INC(PC_INC),
    .PC_REL_CDATA(PC_ADD_CDATA), .PCL_LD_CDATA(PCL_LD_CDATA), .PCL_OUT_CDATA(PCL_OUT_CDATA),
    .PCH_LD_CDATA(PCH_LD_CDATA), .PCH_OUT_CDATA(PCH_OUT_CDATA), .PC_OUT_CADDR(PC_OUT_CADDR),
    .STASHL_LD_CDATA(STASHL_LD_CDATA), .STASHL_OUT_CDATA(STASHL_OUT_CDATA),
    .STASHH_LD_CDATA(STASHH_LD_CDATA), .STASHH_OUT_CDATA(STASHH_OUT_CDATA), .A_LD_CDATA(A_LD_CDATA),
    .A_OUT_CDATA(A_OUT_CDATA), .X_LD_CDATA(X_LD_CDATA), .X_OUT_CDATA(X_OUT_CDATA), .Y_LD_CDATA(Y_LD_CDATA),
    .Y_OUT_CDATA(Y_OUT_CDATA), .PN_LD(PN_LD), .PV_LD(PV_LD), .PZ_LD(PZ_LD), .PC_LD(PC_LD), .P_SRC_0(P_SRC_0),
    .P_SRC_1(P_SRC_1), .ALUA_LD_CDATA(ALUA_LD_CDATA), .ALUB_LD_CDATA(ALUB_LD_CDATA), .ALUC_LD(ALUC_LD),
    .ALUR_OUT_CDATA(ALUR_OUT_CDATA), .ALUOP_0(ALUOP_0), .ALUOP_1(ALUOP_1), .ALUOP_2(ALUOP_2), .S_INC(S_INC),
    .S_DEC(S_DEC), .S_LD_CDATA(S_LD_CDATA), .S_OUT_CDATA(S_OUT_CDATA), .S_OUT_CADDR(S_OUT_CADDR),
    .ALUC_SRC_0(ALUC_SRC_0), .ALUC_SRC_1(ALUC_SRC_1), .CUP_SRC_ALU(CUP_SRC_ALU), .ALUOP_3(ALUOP_3),
    .PC_RESET(ERR));  // open: P_SRC_2, P_OUT_CDATA, P_IRQ, ERR
  LED plus_1 (.in(decoder_1_out_0));
  LED p0 (.in(decoder_1_out_1));
  LED p1 (.in(decoder_1_out_2));
  LED p2 (.in(decoder_1_out_3));
  LED uJMPs (.in(or_6_out));
  assign CADDRH = S_OUT_CADDR ? 8'h1 : 8'bz;  // Driver driver_6
  Instruction_Decoder instruction_decoder_1 (.OPCODE(IR), .DEMODE(DEMODE), .DECOPCODE(DEOPCODE));
  assign CADDRL = S_OUT_CADDR ? S : 8'bz;  // Driver driver_7
  Register u_STASHL (.C(Clck1), .D(CDATA), .OUT(STASHL_OUT_CDATA), .LD(STASHL_LD_CDATA), .Q(CDATA), .lt_Q_gt(STASHL));
  assign CDATA = S_OUT_CDATA ? S : 8'bz;  // Driver driver_8
  Register u_A (.C(Clck1), .D(CDATA), .OUT(A_OUT_CDATA), .LD(A_LD_CDATA), .Q(CDATA), .lt_Q_gt(A));
  PC pc_2 (
    .LDH(PCH_LD_CDATA), .LDL(PCL_LD_CDATA), .INC(PC_INC), .ADD(PC_ADD_CDATA), .D(CDATA), .C(Clck1), .QH(PCH),
    .QL(PCL));
  Register u_X (.C(Clck1), .D(CDATA), .OUT(X_OUT_CDATA), .LD(X_LD_CDATA), .Q(CDATA), .lt_Q_gt(X));
  assign CDATA = PCH_OUT_CDATA ? PCH : 8'bz;  // Driver driver_9
  assign CADDRH = PC_OUT_CADDR ? PCH : 8'bz;  // Driver driver_10
  Register u_Y (.C(Clck1), .D(CDATA), .OUT(Y_OUT_CDATA), .LD(Y_LD_CDATA), .Q(CDATA), .lt_Q_gt(Y));
  assign CADDRL = PC_OUT_CADDR ? PCL : 8'bz;  // Driver driver_11
  assign CDATA = PCL_OUT_CDATA ? PCL : 8'bz;  // Driver driver_12
  assign CDATA = CDATA_LD_0 ? {8{1'b0}} : 8'bz;  // Driver driver_13
  assign CDATA = CDATA_LD_FF ? {8{1'b1}} : 8'bz;  // Driver driver_14

  // Notes on the sheet:
  //   clk: Hz: 100
  //   Clock
  //   CPU
  //   MAR
  //   A
  //   X
  //   MBR
  //   Y
  //   PC
  //   P
  //   N
  //   IR
  //   V
  //   Z
  //   ROM/RAM Interfacing
  //   STASHL
  //   C
  //   XADDR Bus
  //   CADDRH Bus
  //   CADDRL Bus
  //   STASH
  //   HALTED
  //   ERROR
  //   S
  //   Bank Selection
  //   Instruction Decoder
  //   (p1) Decoded Mode
  //   ALU
  //   ALUA
  //   ALUB
  //   ROM/RAM Banks
  //   Status Flags Processing
  //   P load source
  //   00 reset
  //   01 set
  //   10 ALU
  //   11 Processed CDATA
  //   ALUC
  //   (p2) Decoded OpCode
  //   XDATA Bus
  //   CDATA Bus
  //   ALUOUT
  //   contents of ROM (hex, n*v repeats v):
  //   a9,42
  //   ALU operation
  //   0 0 0 0 AND
  //   0 0 0 1 OR
  //   0 0 1 0 NOT
  //   0 0 1 1 XOR
  //   0 1 0 0 ADD
  //   0 1 0 1 SUB
  //   0 1 1 0 INC
  //   0 1 1 1 DEC
  //   1 0  0 0 SHIFT-R
  //   1 0 0 1 SHIFT-L
  //   1 0 1 0 ROT-R
  //   1 0 1 1 ROT-L
  //   ALUC Load Source
  //   0 0   0
  //   0 1   1
  //   1 0   P
  //   1 1    P
  //   Control Unit
  //   uCAR
  //   uNext CAR
  //   uParam
  //   S (Stack Pointer)
  //   In/out CDATA out CADDR
  //   NextMux
  //   General Purpose Registers
  //   PC - In/out CDATA out CADDR
  //   Used for initialisation/reset
endmodule
