// Digital circuit Control Unit.dig as structural Verilog
module Control_Unit (
  input  Nin,
  input  Vin,
  input  Zin,
  input  Cin,
  input  [7:0] IRin,
  input  ClockIn,
  input  RESET,
  output HALT,
  output MEM_LD_XDATA,
  output MEM_OUT_XDATA,
  output IR_LD_XDATA,
  output MBR_LD_XDATA,
  output MBR_OUT_XDATA,
  output MBR_LD_CDATA,
  output MBR_OUT_CDATA,
  output MARL_LD_CADDRL,
  output MARH_LD_CADDRH,
  output PCL_LD_CDATA,
  output PCH_LD_CDATA,
  output PC_INC,
  output PC_LD_ADD,
  output PC_OUT_CADDR,
  output PCL_LD_CADDRL,
  output PCH_LD_CADDRH,
  output STASHH_LD_CDATA,
  output STASHH_OUT_CDATA,
  output A_LD_CDATA,
  output A_OUT_CDATA,
  output X_LDCDATA,
  output X_OUT_CDATA,
  output Y_LD_CDATA,
  output Y_OUT_CDATA,
  output PN_LD,
  output PV_LD,
  output PZ_LD,
  output PC_LD,
  output P_SRC_0,
  output P_SRC_1,
  output ALUA_LD_CDATA,
  output ALU_B_LD_CDATA,
  output ALUP_LD_P,
  output ALUR_OUT_CDATA,
  output ALU_OP_0,
  output ALU_OP_1,
  output ALU_OP_2,
  output [15:0] lt_CAR_gt,
  output [15:0] lt_UNEXTADDR_gt,
  output [15:0] lt_NEXT_gt,
  output [2:0] lt_NEXTMUX_gt,
  output [15:0] lt_MODEMAP_gt,
  output [15:0] lt_OPCODEMAP_gt,
  output S_INC,
  output S_DEC,
  output S_OUT_ADDR,
  output S_LD_CDATA,
  output CDATA_LD_0,
  output CDATA_LD_FF,
  output S_OUT_CDATA,
  output PCL_OUT_CDATA,
  output PCH_OUT_CDATA,
  output STASHL_LD_CDATA,
  output STASHL_OUT_CDATA,
  output CDATA_TO_CADDRL,
  output CDATA_TO_CADDRH
);

  wire and_1_out, and_2_out, and_3_out, and_4_out, uCJMP, uJMP, uJMPINV, uNJMP, uP0, uP0_LD_UNEXTADDR, uP1,
       uP2, uVJMP, uZJMP, xor_1_out, xor_2_out, xor_3_out, xor_4_out;
  wire [15:0] add_1_s, multiplexer_2_out, p0__Fetch_q;
  wire [15:13] uCode_4_d;

  Seven_Seg_Hex seven_seg_hex_1 (.d(lt_CAR_gt[15:12]), .dp(1'b0));
  Seven_Seg_Hex seven_seg_hex_2 (.d(lt_UNEXTADDR_gt[15:12]), .dp(1'b0));
  Seven_Seg_Hex seven_seg_hex_3 (.d(lt_CAR_gt[7:4]), .dp(1'b0));
  Seven_Seg_Hex seven_seg_hex_4 (.d(lt_CAR_gt[11:8]), .dp(1'b0));
  Seven_Seg_Hex seven_seg_hex_5 (.d(lt_UNEXTADDR_gt[7:4]), .dp(1'b0));
  Seven_Seg_Hex seven_seg_hex_6 (.d(lt_UNEXTADDR_gt[11:8]), .dp(1'b0));
  LED led_1 (.in(lt_NEXTMUX_gt[1]));
  LED led_2 (.in(lt_NEXTMUX_gt[2]));
  Seven_Seg_Hex seven_seg_hex_7 (.d(lt_CAR_gt[3:0]), .dp(1'b0));
  Seven_Seg_Hex seven_seg_hex_8 (.d(lt_UNEXTADDR_gt[3:0]), .dp(1'b0));
  LED led_3 (.in(lt_NEXTMUX_gt[0]));
  Seven_Seg_Hex seven_seg_hex_9 (.d(lt_NEXT_gt[11:8]), .dp(1'b0));
  Seven_Seg_Hex seven_seg_hex_10 (.d(lt_NEXT_gt[15:12]), .dp(1'b0));
  Seven_Seg_Hex seven_seg_hex_11 (.d(lt_NEXT_gt[3:0]), .dp(1'b0));
  Seven_Seg_Hex seven_seg_hex_12 (.d(lt_NEXT_gt[7:4]), .dp(1'b0));
  ROM #(.AddrBits(16), .Bits(16)) uCode0 (.A(lt_CAR_gt), .sel(1'b1), .D(lt_UNEXTADDR_gt));
  ROM #(.AddrBits(16), .Bits(16)) uCode1 (
    .A(lt_CAR_gt), .sel(1'b1),
    .D({MBR_LD_CDATA, MBR_OUT_XDATA, MBR_LD_XDATA, IR_LD_XDATA, MEM_OUT_XDATA, MEM_LD_XDATA, HALT, uJMPINV, uCJMP, uZJMP, uVJMP, uNJMP, uJMP, uP2, uP1, uP0}));
  ROM #(.AddrBits(16), .Bits(16)) uCode2 (
    .A(lt_CAR_gt), .sel(1'b1),
    .D({X_OUT_CDATA, X_LDCDATA, A_OUT_CDATA, A_LD_CDATA, STASHH_OUT_CDATA, STASHH_LD_CDATA, PCH_LD_CADDRH, PCL_LD_CADDRL, PC_OUT_CADDR, PC_LD_ADD, PC_INC, PCH_LD_CDATA, PCL_LD_CDATA, MARH_LD_CADDRH, MARL_LD_CADDRL, MBR_OUT_CDATA}));
  ROM #(.AddrBits(16), .Bits(16)) uCode_3 (
    .A(lt_CAR_gt), .sel(1'b1),
    .D({S_INC, ALU_OP_2, ALU_OP_1, ALU_OP_0, ALUR_OUT_CDATA, ALUP_LD_P, ALU_B_LD_CDATA, ALUA_LD_CDATA, P_SRC_1, P_SRC_0, PC_LD, PZ_LD, PV_LD, PN_LD, Y_OUT_CDATA, Y_LD_CDATA}));
  ROM #(.AddrBits(16), .Bits(16)) uCode_4 (
    .A(lt_CAR_gt), .sel(1'b1),
    .D({uCode_4_d, CDATA_TO_CADDRH, CDATA_TO_CADDRL, STASHL_OUT_CDATA, STASHL_LD_CDATA, PCH_OUT_CDATA, PCL_OUT_CDATA, S_OUT_CDATA, CDATA_LD_FF, uP0_LD_UNEXTADDR, CDATA_LD_0, S_LD_CDATA, S_OUT_ADDR, S_DEC}));
  Add #(.Bits(16)) add_1 (.a(lt_CAR_gt), .b(16'h1), .c_i(1'b0), .s(add_1_s));  // open: c_o
  Register #(.Bits(16)) CAR (.D(lt_NEXT_gt), .C(ClockIn), .en(1'b1), .Q(lt_CAR_gt));
  Register #(.Bits(16)) p0__Fetch (.D(lt_UNEXTADDR_gt), .C(ClockIn), .en(uP0_LD_UNEXTADDR), .Q(p0__Fetch_q));
  ROM #(.AddrBits(8), .Bits(16)) p1__Mode (.A(IRin), .sel(1'b1), .D(lt_MODEMAP_gt));
  ROM #(.AddrBits(8), .Bits(16)) p2__OpCode (.A(IRin), .sel(1'b1), .D(lt_OPCODEMAP_gt));
  and and_1 (and_1_out, uZJMP, xor_1_out);
  xor xor_1 (xor_1_out, Zin, uJMPINV);
  or or_1 (lt_NEXTMUX_gt[2], uJMP, and_1_out, and_2_out, and_3_out, and_4_out);
  and and_2 (and_2_out, uNJMP, xor_2_out);
  xor xor_2 (xor_2_out, Nin, uJMPINV);
  and and_3 (and_3_out, uVJMP, xor_3_out);
  xor xor_3 (xor_3_out, Vin, uJMPINV);
  Multiplexer #(.Bits(16)) multiplexer_1 (.sel(RESET), .in_0(multiplexer_2_out), .in_1({16{1'b0}}), .out(lt_NEXT_gt));
  and and_4 (and_4_out, uCJMP, xor_4_out);
  xor xor_4 (xor_4_out, Cin, uJMPINV);
  Multiplexer #(.Selector_Bits(3), .Bits(16)) multiplexer_2 (
    .sel(lt_NEXTMUX_gt), .in_0(add_1_s), .in_1(p0__Fetch_q), .in_2(lt_MODEMAP_gt), .in_3(lt_OPCODEMAP_gt),
    .in_4(lt_UNEXTADDR_gt), .in_5({16{1'b0}}), .in_6({16{1'b0}}), .in_7({16{1'b0}}), .out(multiplexer_2_out));
  or or_2 (lt_NEXTMUX_gt[1], uP1, uP2);
  or or_3 (lt_NEXTMUX_gt[0], uP0, uP2);

  // Other names for the same wires on the sheet: X_LD_CDATA = X_LDCDATA; ALUB_LD_CDATA = ALU_B_LD_CDATA;
  //   ALUOP_0 = ALU_OP_0; ALUOP_1 = ALU_OP_1; ALUOP_2 = ALU_OP_2; S_OUT_CADDR = S_OUT_ADDR;
  //   NextMux[2:0] = lt_NEXTMUX_gt; CAR[15:0] = lt_CAR_gt; Clock = ClockIn; ModeMap[15:0] = lt_MODEMAP_gt;
  //   Next[15:0] = lt_NEXT_gt; OpCodeMap[15:0] = lt_OPCODEMAP_gt; uNextAddr[15:0] = lt_UNEXTADDR_gt

  // Notes on the sheet:
  //   IRin: default 169
  //   CAR
  //   uNextAddr
  //   NextMux
  //   Next
  //   Next Mux
  //   0 0 0 +1
  //   0 0 1 p0 (0)
  //   0 1 0 p1
  //   0 1 1 p2
  //   1 X X uJMPs
  //   Debug
  //   contents of uCode0 (hex, n*v repeats v):
  //   6000000,18000000,6000000,30000000,c0000000
  //   contents of uCode1 (hex, n*v repeats v):
  //   6000000,18000000,6000000,30000000,c0000000
  //   contents of uCode2 (hex, n*v repeats v):
  //   6000000,18000000,6000000,30000000,c0000000
  //   contents of uCode_3 (hex, n*v repeats v):
  //   6000000,18000000,6000000,30000000,c0000000
  //   contents of uCode_4 (hex, n*v repeats v):
  //   6000000,18000000,6000000,30000000,c0000000
  //   contents of p1__Mode (hex, n*v repeats v):
  //   6000000,18000000,6000000,30000000,c0000000
  //   contents of p2__OpCode (hex, n*v repeats v):
  //   6000000,18000000,6000000,30000000,c0000000
endmodule
