// Digital circuit Latched ALU.dig as structural Verilog
module Latched_ALU (
  input  Clock,
  input  [7:0] A,
  input  [7:0] B,
  input  Cin,
  input  LDA,
  input  LDB,
  input  LDC,
  input  [2:0] OP,
  output N,
  output V,
  output Z,
  output C,
  output [7:0] R,
  output [7:0] lt_A_gt,
  output [7:0] lt_B_gt,
  output lt_C_gt
);

  Register #(.Bits(8)) u_A (.D(A), .C(Clock), .en(LDA), .Q(lt_A_gt));
  Register #(.Bits(8)) u_B (.D(B), .C(Clock), .en(LDB), .Q(lt_B_gt));
  Register u_C (.D(Cin), .C(Clock), .en(LDC), .Q(lt_C_gt));
  ALU ALU (.A(lt_A_gt), .B(lt_B_gt), .OP(OP), .Cin(lt_C_gt), .Out(R), .Nout(N), .Vout(V), .Zout(Z), .Cout(C));

  // Notes on the sheet:
  //   ALU operation
  //   0 0 0 0 AND
  //   0 0 0 1 OR
  //   0 0 1 0 NOT
  //   0 0 1 1 XOR
  //   0 1 0 0 ADD
  //   0 1 0 1 SUB
  //   0 1 1 0 INC
  //   0 1 1 1 DEC
  //   1 0  0 0 SHIFT-R
  //   1 0 0 1 SHIFT-L
  //   1 0 1 0 ROT-R
  //   1 0 1 1 ROT-L
endmodule
