// Digital circuit PC.dig as structural Verilog
module PC (
  input  LDH,
  input  LDL,
  input  INC,
  input  ADD,
  input  [7:0] D,
  input  C,
  input  RESET,
  output [7:0] QH,
  output [7:0] QL
);

  wire and_1_out, or_1_out, or_2_out, PCADDL_c_o;
  wire [7:0] multiplexer_1_out, multiplexer_2_out, multiplexer_3_out, multiplexer_4_out, PCADDH_s, PCADDL_s;

  Multiplexer #(.Selector_Bits(2), .Bits(8)) multiplexer_1 (
    .sel({RESET, LDH}), .in_0(PCADDH_s), .in_1(D), .in_2({8{1'b1}}), .in_3({8{1'b0}}), .out(multiplexer_1_out));
  or or_1 (or_1_out, INC, ADD, LDH, RESET);
  and and_1 (and_1_out, D[7], ADD);
  Register #(.Bits(8)) PCH (.D(multiplexer_1_out), .C(C), .en(or_1_out), .Q(QH));
  Multiplexer #(.Bits(8)) multiplexer_2 (.sel(and_1_out), .in_0({8{1'b0}}), .in_1({8{1'b1}}), .out(multiplexer_2_out));
  Add #(.Bits(8)) PCADDH (.a(QH), .b(multiplexer_2_out), .c_i(PCADDL_c_o), .s(PCADDH_s));  // open: c_o
  Multiplexer #(.Selector_Bits(2), .Bits(8)) multiplexer_3 (
    .sel({RESET, LDL}), .in_0(PCADDL_s), .in_1(D), .in_2(8'hfc), .in_3({8{1'b0}}), .out(multiplexer_3_out));
  Multiplexer #(.Bits(8)) multiplexer_4 (.sel(INC), .in_0(D), .in_1(8'h1), .out(multiplexer_4_out));
  Add #(.Bits(8)) PCADDL (.a(QL), .b(multiplexer_4_out), .c_i(1'b0), .s(PCADDL_s), .c_o(PCADDL_c_o));
  or or_2 (or_2_out, INC, ADD, LDL, RESET);
  Register #(.Bits(8)) PCL (.D(multiplexer_3_out), .C(C), .en(or_2_out), .Q(QL));
endmodule
